// Logisim project controlLogic.circ as structural Verilog: 2 circuits, main circuit AluControl
module AluControl (
  input  [1:0] ALUOp,
  input  [5:0] Func,
  output [3:0] ALUcon
);

  wire and_1_out, and_2_out, and_3_out, not_1_out, not_2_out, not_3_out, or_1_out;

  and and_1 (and_1_out, ALUOp[1], Func[1]);
  not not_1 (not_1_out, Func[1]);
  and and_2 (and_2_out, Func[2], Func[1], Func[0]);
  and and_3 (and_3_out, not_1_out, Func[0]);
  or or_1 (or_1_out, Func[3], and_3_out);
  and and_4 (ALUcon[3], ALUOp[1], and_2_out);
  or or_2 (ALUcon[2], ALUOp[0], and_1_out);
  not not_2 (not_2_out, ALUOp[1]);
  or or_3 (ALUcon[1], not_2_out, ALUOp[0], not_3_out);
  not not_3 (not_3_out, Func[2]);
  and and_5 (ALUcon[0], ALUOp[1], or_1_out);
endmodule

module MainControl (
  input  [5:0] opcode,
  output Branch,
  output RegDst,
  output MemRead,
  output MemToReg,
  output [1:0] ALUop,
  output MemWrite,
  output ALUsrc,
  output RegWrite
);

  wire addi_out, not_1_out, not_2_out, not_3_out, not_4_out, not_5_out, not_6_out, not_7_out, not_8_out,
       not_9_out, not_10_out, not_11_out, not_12_out, not_13_out, not_14_out, not_15_out, not_16_out,
       not_17_out, not_18_out, not_19_out, not_20_out, not_21_out;

  not not_1 (not_1_out, opcode[5]);
  not not_2 (not_2_out, opcode[4]);
  not not_3 (not_3_out, opcode[3]);
  not not_4 (not_4_out, opcode[0]);
  not not_5 (not_5_out, opcode[2]);
  not not_6 (not_6_out, opcode[1]);
  and R_format (ALUop[1], not_1_out, not_2_out, not_3_out, not_5_out, not_6_out, not_4_out);
  not not_7 (not_7_out, opcode[2]);
  not not_8 (not_8_out, opcode[3]);
  not not_9 (not_9_out, opcode[4]);
  and lw (MemRead, opcode[5], not_9_out, not_8_out, not_7_out, opcode[1], opcode[0]);
  not not_10 (not_10_out, opcode[4]);
  not not_11 (not_11_out, opcode[2]);
  and sw (MemWrite, opcode[5], not_10_out, opcode[3], not_11_out, opcode[1], opcode[0]);
  not not_12 (not_12_out, opcode[4]);
  not not_13 (not_13_out, opcode[5]);
  not not_14 (not_14_out, opcode[3]);
  and beq (ALUop[0], not_13_out, not_12_out, not_14_out, opcode[2], not_18_out, not_17_out);
  not not_15 (not_15_out, opcode[5]);
  not not_16 (not_16_out, opcode[4]);
  not not_17 (not_17_out, opcode[0]);
  not not_18 (not_18_out, opcode[1]);
  not not_19 (not_19_out, opcode[0]);
  not not_20 (not_20_out, opcode[2]);
  not not_21 (not_21_out, opcode[1]);
  and addi (addi_out, not_15_out, not_16_out, opcode[3], not_20_out, not_21_out, not_19_out);
  or or_1 (RegWrite, MemRead, addi_out, ALUop[1]);
  or or_2 (ALUsrc, MemRead, addi_out, MemWrite);

  assign Branch = ALUop[0];
  assign MemToReg = MemRead;
  assign RegDst = ALUop[1];
endmodule
