// Logisim project mipsProcessor.circ as structural Verilog: 3 circuits, main circuit main
module main (
);

  wire and_1_out, Clock_out, main_1_zero, maincontrol_1_alusrc, maincontrol_1_branch, maincontrol_1_memread,
       maincontrol_1_memtoreg, maincontrol_1_memwrite, maincontrol_1_regdst, maincontrol_1_regwrite;
  wire [1:0] maincontrol_1_aluop;
  wire [3:0] alucontrol_1_alucon;
  wire [4:0] multiplexer_1_out;
  wire [31:0] adder_1_out, adder_2_out, main_1_result, multiplexer_2_out, multiplexer_3_out,
       multiplexer_4_out, PC_q, ram_1_data, registerfile_1_readdata1, registerfile_1_readdata2, rom_1_data,
       shiftlefttwo_1_out_2, signextend_1_out_2;

  Register #(.width(32), .trigger("falling")) PC (.D(multiplexer_2_out), .Q(PC_q), .clk(Clock_out));  // open: en, clr
  Adder #(.width(32)) adder_1 (.a(PC_q), .b(32'h4), .out(adder_1_out));  // open: cin, cout
  Clock Clock (.out(Clock_out));
  ROM #(.addrWidth(6), .dataWidth(32)) rom_1 (.addr(PC_q[7:2]), .data(rom_1_data));  // open: sel
  MainControl maincontrol_1 (
    .opcode(rom_1_data[31:26]), .Branch(maincontrol_1_branch), .RegDst(maincontrol_1_regdst),
    .MemRead(maincontrol_1_memread), .MemToReg(maincontrol_1_memtoreg), .ALUop(maincontrol_1_aluop),
    .MemWrite(maincontrol_1_memwrite), .ALUsrc(maincontrol_1_alusrc), .RegWrite(maincontrol_1_regwrite));
  Multiplexer #(.width(5), .enable("false")) multiplexer_1 (
    .in0(rom_1_data[20:16]), .in1(rom_1_data[15:11]), .out(multiplexer_1_out), .sel(maincontrol_1_regdst));
  Adder #(.width(32)) adder_2 (.a(adder_1_out), .b(shiftlefttwo_1_out_2), .out(adder_2_out));  // open: cin, cout
  shiftLeftTwo shiftlefttwo_1 (.in_1(signextend_1_out_2), .out_2(shiftlefttwo_1_out_2));
  registerFile registerfile_1 (
    .ReadRegister1(rom_1_data[25:21]), .ReadRegister2(rom_1_data[20:16]), .WriteRegister(multiplexer_1_out),
    .WriteData(multiplexer_4_out), .RegWrite(maincontrol_1_regwrite), .Clock(Clock_out),
    .ReadData1(registerfile_1_readdata1), .ReadData2(registerfile_1_readdata2));
  signExtend signextend_1 (.in_1(rom_1_data[15:0]), .out_2(signextend_1_out_2));
  Multiplexer #(.width(32), .enable("false")) multiplexer_2 (
    .in0(adder_1_out), .in1(adder_2_out), .out(multiplexer_2_out), .sel(and_1_out));
  and and_1 (and_1_out, maincontrol_1_branch, main_1_zero);
  Multiplexer #(.width(32), .enable("false")) multiplexer_3 (
    .in0(registerfile_1_readdata2), .in1(signextend_1_out_2), .out(multiplexer_3_out),
    .sel(maincontrol_1_alusrc));
  AluControl alucontrol_1 (.ALUOp(maincontrol_1_aluop), .Func(rom_1_data[5:0]), .ALUcon(alucontrol_1_alucon));
  mipsalu_main main_1 (
    .A(registerfile_1_readdata1), .B(multiplexer_3_out), .Ainvert(alucontrol_1_alucon[3]),
    .Bnegate(alucontrol_1_alucon[2]), .Operation(alucontrol_1_alucon[1:0]), .Zero(main_1_zero),
    .Result(main_1_result));
  RAM #(.addrWidth(6), .dataWidth(32), .bus("separate")) ram_1 (
    .addr(main_1_result[7:2]), .din(registerfile_1_readdata2), .data(ram_1_data),
    .str(maincontrol_1_memwrite), .clk(Clock_out), .ld(maincontrol_1_memread));  // open: sel, clr
  Multiplexer #(.width(32), .enable("false")) multiplexer_4 (
    .in0(main_1_result), .in1(ram_1_data), .out(multiplexer_4_out), .sel(maincontrol_1_memtoreg));

  // Notes on the sheet:
  //   contents of rom_1 (hex, n*v repeats v):
  //   22 8c010000 8c220000 8c230004 432024 432825 ac040004 ac050008 1000ffff
endmodule

module shiftLeftTwo (
  input  [31:0] in_1,
  output [31:0] out_2
);


  assign out_2 = {in_1[29:0], 2'b00};
endmodule

module signExtend (
  input  [15:0] in_1,
  output [31:0] out_2
);


  assign out_2 = {{17{in_1[15]}}, in_1[14:0]};
endmodule
