// Logisim project mipsalu.circ as structural Verilog: 2 circuits, main circuit main
module main (
  input  Ainvert,
  input  Bnegate,
  input  [1:0] Operation,
  input  [31:0] A,
  input  [31:0] B,
  output Zero,
  output [31:0] Result
);

  wire [31:0] adder_1_out, and_1_out, multiplexer_1_out, multiplexer_2_out, not_1_out, not_2_out, or_1_out;

  assign not_1_out = ~A;  // NOT_Gate not_1, 32 bits wide
  assign not_2_out = ~B;  // NOT_Gate not_2, 32 bits wide
  Multiplexer #(.width(32), .enable("false")) multiplexer_1 (
    .in0(A), .in1(not_1_out), .out(multiplexer_1_out), .sel(Ainvert));
  Multiplexer #(.width(32), .enable("false")) multiplexer_2 (
    .in0(B), .in1(not_2_out), .out(multiplexer_2_out), .sel(Bnegate));
  assign and_1_out = multiplexer_1_out & multiplexer_2_out;  // AND_Gate and_1, 32 bits wide
  assign or_1_out = multiplexer_1_out | multiplexer_2_out;  // OR_Gate or_1, 32 bits wide
  Adder #(.width(32)) adder_1 (
    .a(multiplexer_1_out), .b(multiplexer_2_out), .out(adder_1_out), .cin(Bnegate));  // open: cout
  zeroGenerator zerogenerator_1 (.result(adder_1_out), .Zero(Zero));
  Multiplexer #(.select(2), .width(32), .enable("false")) multiplexer_3 (
    .in0(and_1_out), .in1(or_1_out), .in2(adder_1_out), .in3({{31{1'b0}}, adder_1_out[31]}), .out(Result),
    .sel(Operation));

  // Notes on the sheet:
  //   The constant represents the less inputs, everything is zero except for the least significant bit which can be 1 if A < B
endmodule

module zeroGenerator (
  input  [31:0] result,
  output Zero
);

  wire or_1_out, or_2_out, or_3_out, or_4_out, or_5_out, or_6_out, or_7_out, or_8_out, or_9_out, or_10_out,
       or_11_out, or_12_out, or_13_out, or_14_out, or_15_out, or_16_out, or_17_out, or_18_out, or_19_out,
       or_20_out, or_21_out, or_22_out, or_23_out, or_24_out, or_25_out, or_26_out, or_27_out, or_28_out,
       or_29_out, or_30_out, or_31_out;

  or or_1 (or_1_out, result[0], result[1]);
  or or_2 (or_2_out, result[2], result[3]);
  or or_3 (or_3_out, result[4], result[5]);
  or or_4 (or_4_out, result[6], result[7]);
  or or_5 (or_5_out, result[8], result[9]);
  or or_6 (or_6_out, result[10], result[11]);
  or or_7 (or_7_out, result[12], result[13]);
  or or_8 (or_8_out, result[14], result[15]);
  or or_9 (or_9_out, result[16], result[17]);
  or or_10 (or_10_out, result[18], result[19]);
  or or_11 (or_11_out, result[20], result[21]);
  or or_12 (or_12_out, result[22], result[23]);
  or or_13 (or_13_out, result[24], result[25]);
  or or_14 (or_14_out, result[26], result[27]);
  or or_15 (or_15_out, result[28], result[29]);
  or or_16 (or_16_out, result[30], result[31]);
  or or_17 (or_17_out, or_1_out, or_2_out);
  or or_18 (or_18_out, or_3_out, or_4_out);
  or or_19 (or_19_out, or_5_out, or_6_out);
  or or_20 (or_20_out, or_7_out, or_8_out);
  or or_21 (or_21_out, or_9_out, or_10_out);
  or or_22 (or_22_out, or_11_out, or_12_out);
  or or_23 (or_23_out, or_13_out, or_14_out);
  or or_24 (or_24_out, or_15_out, or_16_out);
  or or_25 (or_25_out, or_17_out, or_18_out);
  or or_26 (or_26_out, or_19_out, or_20_out);
  or or_27 (or_27_out, or_21_out, or_22_out);
  or or_28 (or_28_out, or_23_out, or_24_out);
  or or_29 (or_29_out, or_25_out, or_26_out);
  or or_30 (or_30_out, or_27_out, or_28_out);
  or or_31 (or_31_out, or_29_out, or_30_out);
  not not_1 (Zero, or_31_out);
endmodule
